# Fritzing sketch only-usage (saved by Fritzing 0.9.3b)
circuit board: 8.46667cm x 5.64444cm
perfboards: 1

parts:
  J1 = female pin header, 4 pins [form="♀ (female)"]
  ESP-01_Connector = female pin header, 4 pins [form="♀ (female)"]
  Serial_2 = female pin header, 2 pins [form="♀ (female)"]  # not connected
  U1 = V_REG_LD1117VXX [package=78xxl]
  VCC_-_GND = Battery block 9V
  Serial = female pin header, 4 pins [form="♀ (female)"]  # not connected
  C2 = Electrolytic Capacitor [capacitance=10µF package="100 mil [THT, electrolytic]"]

nets:
  N1: J1.pin2, ESP-01_Connector.pin1, ESP-01_Connector.pin3, U1.OUT, C2.+
  N2: J1.pin4, U1.GND, VCC_-_GND.-, C2.-
  N3: U1.IN, VCC_-_GND.+
